# Fritzing sketch poulailler_schema (saved by Fritzing 0.9.2b)
circuit board: 4.06427cm x 4.0262cm

parts:
  Composant1 = DeuLigne 1.1 - The Snootlab's LCD shield for Arduino
  R1 = Resistor [tolerance=±5% resistance=220 package=THT]
  R2 = Resistor [tolerance=±5% resistance=220 package=THT]
  R3 = Resistor [tolerance=±5% resistance=220 package=THT]
  Arduino = Arduino Mini (Rev5)
  bas = Pushbutton [package=THT]
  haut = Pushbutton [package=THT]
  driver_moteur = Dual VNH2SP30 Motor Driver
  M1 = DC Motor
  VCC1 = Battery block 9V
  régulateur_5V = Voltage Regulator - 5V [package="TO220 [THT]"]
  cellule_photoelectrique = Photocell (LDR) [package=THT]
  RTC_DS1307 = Real Time Clock Module - DS1307 RTC Breakout Board

nets:
  N1: Composant1.A0, Arduino.A1
  N2: Composant1.D8, Arduino.D3_PWM
  N3: Composant1.D9, Arduino.D4
  N4: Composant1.D10_SS, Arduino.D2
  N5: Composant1.D4, Arduino.D5_PWM
  N6: Composant1.D5, Arduino.D6_PWM
  N7: Composant1.D6, Arduino.D7
  N8: Composant1.D7, Arduino.D8
  N9: Composant1.RESET, Arduino.A2
  GND: R1.Pin_0, R2.Pin_0, Arduino.GND, RTC_DS1307.GND
  N10: R1.Pin_1, Arduino.D9_PWM, bas.leg0
  N11: R2.Pin_1, Arduino.D10_PWM, haut.leg0
  N12: R3.Pin_0, driver_moteur.GND#136, VCC1.-, régulateur_5V.GND
  N13: Arduino.5V, bas.leg1, haut.leg1
  N14: Arduino.A3, cellule_photoelectrique.pin_1
  N15: Arduino.D13, driver_moteur.1DIAG/EN
  N16: Arduino.D12, driver_moteur.1INa
  N17: Arduino.D11_PWM, driver_moteur.1INb
  N18: Arduino.A4, RTC_DS1307.SDA
  N19: Arduino.A5, RTC_DS1307.SCL
  N20: driver_moteur.+5V_(IN), régulateur_5V.output_voltage
  N21: driver_moteur.OUT_1A, M1.pin_1
  N22: driver_moteur.OUT_1B, M1.pin_2
  N23: VCC1.+, régulateur_5V.input_voltage

notes:
  b7 b6 b5 b4 ce rst blight
  + -
  c+ b h i1 i2 en bp rst photo
  cellule
  photoelectrique
  interrupteurs
  A0 = flèches
